# Fritzing sketch arduino_planning (saved by Fritzing 0.9.10b)
breadboards: 1

parts:
  Part1 = Arduino Uno (Rev3)
  RHT1 = Humidity and Temperature Sensor RHT03
  M1 = Stepper Motor - Bipolar
  U1 = L6470 [package=htssop28]
  L1 = Solenoid
  VCC1 = Battery block 9V

nets:
  N1: Part1.D8, U1.STBYN_RESETN
  N2: Part1.D10_PWM/SS, U1.VREG
  N3: Part1.A4/SDA, RHT1.Data-signal
  N4: Part1.A5/SCL, RHT1.Vcc
  N5: Part1.5V, RHT1.GND_1, U1.OUT1A, U1.VSA, U1.OSCOUT, L1.pin2
  N6: Part1.GND, RHT1.GND_2, U1.SW, U1.ADCIN, U1.OSCIN, L1.pin1
  N7: M1.A, U1.OUT2A
  N8: M1.C, U1.FLAGN
  N9: M1.B, U1.PGNDA
  N10: M1.D, U1.CSN
  N11: U1.BUSYN_SYNC, U1.EPAD, VCC1.+
  N12: U1.STCK, U1.VSA2, VCC1.-
